# Fritzing sketch electrochemicalprobe (saved by Fritzing 0.9.2b)

parts:
  Part1 = Arduino Pro Mini v13
  C1 = Ceramic Capacitor [capacitance=100nF package="100 mil [THT, multilayer]"]
  C2 = Ceramic Capacitor [capacitance=100nF package="100 mil [THT, multilayer]"]
  C3 = Ceramic Capacitor [capacitance=100nF package="100 mil [THT, multilayer]"]

nets:
  N1: Part1.A2, C3.0
  N2: Part1.A1, C2.0
  N3: Part1.A0, C1.0
  N4: C1.1, C2.1, C3.1
